// Logisim project Vrata_Version0.0.1.circ as structural Verilog: 3 circuits, main circuit main
module main (
  output \Levá_zavírání ,
  output \Pravá_zavírání ,
  output \Zavřít_vrata ,
  output ZAPNUTO_VYPNUTO
);

  wire and_2_out, and_3_out, and_4_out, and_5_out, and_6_out, and_7_out, and_8_out, button_1_out,
       clock_1_out, lo, not_1_out, not_2_out, not_3_out, not_4_out, not_5_out, not_6_out, or_1_out, po,
       reset_1_output___reset;

  Clock clock_1 (.out(clock_1_out));
  buttonswitch buttonswitch_1 (.in_2(button_1_out), .out_3(ZAPNUTO_VYPNUTO), .in_1(reset_1_output___reset));
  Button button_1 (.out(button_1_out));
  not not_1 (not_1_out, ZAPNUTO_VYPNUTO);
  and and_1 (\Levá_zavírání , \Pravá_zavírání , po);
  and and_2 (and_2_out, ZAPNUTO_VYPNUTO, clock_1_out);
  Counter #(.width(3), .max('h7), .ongoal("stay")) counter_1 (
    .load(\Levá_zavírání ), .carry(lo), .clk(and_2_out));  // open: D, count, Q, clr
  and and_3 (and_3_out, po, not_2_out);
  not not_2 (not_2_out, \Pravá_zavírání );
  not not_3 (not_3_out, po);
  not not_4 (not_4_out, lo);
  and and_4 (and_4_out, lo, ZAPNUTO_VYPNUTO, clock_1_out);
  not not_5 (not_5_out, \Pravá_zavírání );
  and and_5 (and_5_out, ZAPNUTO_VYPNUTO, not_5_out, not_6_out);
  not not_6 (not_6_out, po);
  and and_6 (and_6_out, not_3_out, \Pravá_zavírání );
  or or_1 (or_1_out, and_6_out, and_7_out);
  and and_7 (and_7_out, not_4_out, \Pravá_zavírání );
  reset reset_1 (
    .Leva_Zavirani(lo), .Leva_Zavreno(\Levá_zavírání ), .Zavrit(\Pravá_zavírání ),
    .OUTPUT___RESET(reset_1_output___reset), .CLOCK(clock_1_out));
  Counter #(.width(3), .max('h7), .ongoal("stay")) counter_2 (
    .load(\Pravá_zavírání ), .carry(po), .clk(and_4_out));  // open: D, count, Q, clr
  LED led_1 (.in(and_5_out));
  LED led_2 (.in(and_3_out));
  LED led_3 (.in(or_1_out));
  LED led_4 (.in(not_1_out));
  and and_8 (and_8_out, po, ZAPNUTO_VYPNUTO, clock_1_out);
  Counter #(.width(3), .max('h7), .ongoal("stay")) counter_3 (
    .carry(\Pravá_zavírání ), .clk(and_8_out), .clr(reset_1_output___reset));  // open: load, D, count, Q

  assign \Zavřít_vrata  = \Pravá_zavírání ;

  // Other names for the same wires on the sheet: zr = \Pravá_zavírání 

  // Notes on the sheet:
  //   START/STOP
  //   otevírání
  //   otevřeno
  //   zavírání
  //   zavřeno
endmodule

module buttonswitch (
  input  in_1,
  input  in_2,
  output out_3
);

  wire d_ff_1_qn, d_ff_2_q, or_1_out;

  or or_1 (or_1_out, in_2, in_1);
  D_Flip_Flop #(.trigger("high")) d_ff_1 (
    .clk(or_1_out), .D(d_ff_2_q), .Q(out_3), .Qn(d_ff_1_qn));  // open: preset, en, reset
  D_Flip_Flop d_ff_2 (.clk(or_1_out), .D(d_ff_1_qn), .Q(d_ff_2_q));  // open: Qn, preset, en, reset
endmodule

module reset (
  input  Leva_Zavirani,
  input  Leva_Zavreno,
  input  Zavrit,
  input  CLOCK,
  output OUTPUT___RESET
);

  wire and_1_out;

  and and_1 (and_1_out, Leva_Zavirani, Leva_Zavreno, Zavrit);
  Counter #(.width(1), .max('h1), .trigger("falling")) counter_1 (
    .count(and_1_out), .carry(OUTPUT___RESET), .clk(CLOCK), .clr(OUTPUT___RESET));  // open: load, D, Q
endmodule
